// Logisim project design_cpu_logisim.circ as structural Verilog
module main (
  input  [2:0] in_1,
  input  [2:0] in_2,
  input  i,
  input  [2:0] in_4,
  input  [2:0] in_5,
  input  s,
  input  [1:0] in_7,
  input  [7:0] in_8,
  input  e,
  input  in_10,
  input  [3:0] in_11,
  input  in_12,
  input  [7:0] in_13,
  input  [7:0] in_14,
  output out_15,
  output [2:0] out_16,
  output out_17,
  output [7:0] out_18,
  output [31:0] out_19,
  output err
);

  wire decoder_1_out0, decoder_1_out1, decoder_1_out2, decoder_1_out3, decoder_1_out4, decoder_1_out5,
       decoder_1_out6, decoder_1_out7, decoder_1_out8, decoder_1_out9, decoder_1_out10, decoder_1_out11,
       decoder_1_out12, decoder_1_out13, decoder_1_out14, decoder_1_out15, not_1_out;
  wire [7:0] ram_1_dout;

  Decoder #(.select(4)) decoder_1 (
    .out0(decoder_1_out0), .out1(decoder_1_out1), .out2(decoder_1_out2), .out3(decoder_1_out3),
    .out4(decoder_1_out4), .out5(decoder_1_out5), .out6(decoder_1_out6), .out7(decoder_1_out7),
    .out8(decoder_1_out8), .out9(decoder_1_out9), .out10(decoder_1_out10), .out11(decoder_1_out11),
    .out12(decoder_1_out12), .out13(decoder_1_out13), .out14(decoder_1_out14), .out15(decoder_1_out15),
    .sel(in_11), .en(e));
  // IntToFP #(.mode("unsigned")) inttofp_1: pin names not known; wires that end beside it: in_14, err, decoder_1_out0, decoder_1_out1, decoder_1_out2, decoder_1_out3, decoder_1_out4, decoder_1_out5, decoder_1_out6, decoder_1_out7, decoder_1_out8, decoder_1_out9, decoder_1_out10, decoder_1_out11, decoder_1_out12, decoder_1_out13, decoder_1_out14, decoder_1_out15, out_19
  Multiplexer #(.select(2), .width(3)) multiplexer_1 (
    .in0(in_1), .in1(in_2), .in2(in_4), .in3(in_5), .out(out_16), .sel(in_7));
  S_R_Flip_Flop s_r_ff_1 (.S(i), .R(not_1_out), .clk(s), .Q(out_15), .Qn(out_17));  // open: reset, preset
  not not_1 (not_1_out, i);
  RAM #(.trigger("high")) ram_1 (.addr(in_8), .we(in_10), .oe(in_12), .din(in_13), .dout(ram_1_dout));
  assign out_18 = in_12 ? ram_1_dout : 8'bz;  // Controlled_Buffer controlled_buffer_1
  D_Flip_Flop d_ff_1 ();  // open: D, clk, Q, Qn, preset, reset
  T_Flip_Flop t_ff_1 ();  // open: T, clk, Q, Qn, reset, preset
  J_K_Flip_Flop j_k_ff_1 ();  // open: J, K, clk, Q, Qn, preset, reset
endmodule

module CPU_MEM_1 (
  input  i,
  input  s,
  output o
);

  wire nand_1_out, nand_2_out, nand_4_out;

  nand nand_1 (nand_1_out, i, s);
  nand nand_2 (nand_2_out, nand_1_out, s);
  nand nand_3 (o, nand_1_out, nand_4_out);
  nand nand_4 (nand_4_out, o, nand_2_out);

  // Notes on the sheet:
  //   o: pull=down
endmodule

module CPU_MEM_8 (
  input  [7:0] i,
  input  s,
  output [7:0] o
);

  CPU_MEM_1 cpu_mem_1_1 (.i(i[0]), .s(s), .o(o[0]));
  CPU_MEM_1 cpu_mem_1_2 (.i(i[1]), .s(s), .o(o[1]));
  CPU_MEM_1 cpu_mem_1_3 (.i(i[2]), .s(s), .o(o[2]));
  CPU_MEM_1 cpu_mem_1_4 (.i(i[3]), .s(s), .o(o[3]));
  CPU_MEM_1 cpu_mem_1_5 (.i(i[4]), .s(s), .o(o[4]));
  CPU_MEM_1 cpu_mem_1_6 (.i(i[5]), .s(s), .o(o[5]));
  CPU_MEM_1 cpu_mem_1_7 (.i(i[6]), .s(s), .o(o[6]));
  CPU_MEM_1 cpu_mem_1_8 (.i(i[7]), .s(s), .o(o[7]));
endmodule

module CPU_ENABLE_8 (
  input  [7:0] i,
  input  e,
  output [7:0] o
);

  wire and_1_out, and_2_out, and_3_out, and_4_out, and_5_out, and_6_out, and_7_out, and_8_out;

  and and_1 (and_1_out, i[0], e);
  and and_2 (and_2_out, i[1], e);
  and and_3 (and_3_out, i[2], e);
  and and_4 (and_4_out, i[3], e);
  and and_5 (and_5_out, i[4], e);
  and and_6 (and_6_out, i[5], e);
  and and_7 (and_7_out, i[6], e);
  and and_8 (and_8_out, i[7], e);
  assign o[0] = e ? and_1_out : 1'bz;  // Controlled_Buffer controlled_buffer_1
  assign o[1] = e ? and_2_out : 1'bz;  // Controlled_Buffer controlled_buffer_2
  assign o[2] = e ? and_3_out : 1'bz;  // Controlled_Buffer controlled_buffer_3
  assign o[3] = e ? and_4_out : 1'bz;  // Controlled_Buffer controlled_buffer_4
  assign o[4] = e ? and_5_out : 1'bz;  // Controlled_Buffer controlled_buffer_5
  assign o[5] = e ? and_6_out : 1'bz;  // Controlled_Buffer controlled_buffer_6
  assign o[6] = e ? and_7_out : 1'bz;  // Controlled_Buffer controlled_buffer_7
  assign o[7] = e ? and_8_out : 1'bz;  // Controlled_Buffer controlled_buffer_8
endmodule

module CPU_REG_8 (
  input  [7:0] i,
  input  s,
  input  e,
  output [7:0] r,
  output [7:0] o
);

  wire [7:0] cpu_enable_8_1_o;

  CPU_MEM_8 cpu_mem_8_1 (.i(i), .s(s), .o(r));
  CPU_ENABLE_8 cpu_enable_8_1 (.i(r), .e(e), .o(cpu_enable_8_1_o));
  assign o = e ? cpu_enable_8_1_o : 8'bz;  // Controlled_Buffer controlled_buffer_1

  // Notes on the sheet:
  //   i: pull=down
  //   o: pull=down
endmodule

module CPU_DECODER_2x4 (
  input  a,
  input  b,
  output o1,
  output o2,
  output o3,
  output o4
);

  wire not_1_out, not_2_out;

  not not_1 (not_1_out, a);
  not not_2 (not_2_out, b);
  and and_1 (o1, not_1_out, not_2_out);
  and and_2 (o2, not_1_out, b);
  and and_3 (o3, a, not_2_out);
  and and_4 (o4, a, b);
endmodule

module CPU_DECODER_3x8 (
  input  a,
  input  b,
  input  c,
  output o1,
  output o2,
  output o3,
  output o4,
  output o5,
  output o6,
  output o7,
  output o8
);

  wire not_1_out, not_2_out, not_3_out;

  not not_1 (not_1_out, a);
  not not_2 (not_2_out, b);
  not not_3 (not_3_out, c);
  and and_1 (o1, not_1_out, not_2_out, not_3_out);
  and and_2 (o2, not_1_out, not_2_out, c);
  and and_3 (o3, not_1_out, b, not_3_out);
  and and_4 (o4, not_1_out, b, c);
  and and_5 (o5, a, not_2_out, not_3_out);
  and and_6 (o6, a, not_2_out, c);
  and and_7 (o7, a, b, not_3_out);
  and and_8 (o8, a, b, c);
endmodule

module CPU_DECODER_4x16 (
  input  [3:0] i,
  output o1,
  output o2,
  output o3,
  output o4,
  output o5,
  output o6,
  output o7,
  output o8,
  output o9,
  output o10,
  output o11,
  output o12,
  output o13,
  output o14,
  output o15,
  output o16
);

  wire not_1_out, not_2_out, not_3_out, not_4_out;

  not not_1 (not_1_out, i[3]);
  not not_2 (not_2_out, i[2]);
  not not_3 (not_3_out, i[1]);
  not not_4 (not_4_out, i[0]);
  and and_1 (o1, not_1_out, not_2_out, not_3_out, not_4_out);
  and and_2 (o2, not_1_out, not_2_out, not_3_out, i[0]);
  and and_3 (o3, not_1_out, not_2_out, i[1], not_4_out);
  and and_4 (o4, not_1_out, not_2_out, i[1], i[0]);
  and and_5 (o5, not_1_out, i[2], not_3_out, not_4_out);
  and and_6 (o6, not_1_out, i[2], not_3_out, i[0]);
  and and_7 (o7, not_1_out, i[2], i[1], not_4_out);
  and and_8 (o8, not_1_out, i[2], i[1], i[0]);
  and and_9 (o9, i[3], not_2_out, not_3_out, not_4_out);
  and and_10 (o10, i[3], not_2_out, not_3_out, i[0]);
  and and_11 (o11, i[3], not_2_out, i[1], not_4_out);
  and and_12 (o12, i[3], not_2_out, i[1], i[0]);
  and and_13 (o13, i[3], i[2], not_3_out, not_4_out);
  and and_14 (o14, i[3], i[2], not_3_out, i[0]);
  and and_15 (o15, i[3], i[2], i[1], not_4_out);
  and and_16 (o16, i[3], i[2], i[1], i[0]);
endmodule

module CPU_REG_BYTE (
  input  reset,
  input  [7:0] i,
  input  h,
  input  v,
  input  s,
  input  e,
  output [7:0] op,
  output [7:0] o
);

  wire and_1_out, and_2_out, and_3_out, or_1_out;
  wire [7:0] cpu_reg_8_1_o;

  and and_1 (and_1_out, h, v);
  and and_2 (and_2_out, and_1_out, s);
  and and_3 (and_3_out, and_1_out, e);
  or or_1 (or_1_out, reset, and_2_out);
  CPU_REG_8 cpu_reg_8_1 (.i(i), .s(or_1_out), .e(and_3_out), .r(op), .o(cpu_reg_8_1_o));
  assign o = and_3_out ? cpu_reg_8_1_o : 8'bz;  // Controlled_Buffer controlled_buffer_1
endmodule

module CPU_RAM_32 (
  input  [7:0] i,
  input  sa,
  input  [7:0] adress,
  input  s,
  input  e,
  input  reset,
  output [7:0] o,
  output [7:0] out_8,
  output [7:0] out_9,
  output [7:0] out_10,
  output [7:0] out_11,
  output [7:0] out_12,
  output [7:0] out_13,
  output [7:0] out_14,
  output [7:0] out_15,
  output [7:0] out_16,
  output [7:0] out_17,
  output [7:0] out_18,
  output [7:0] out_19,
  output [7:0] out_20,
  output [7:0] out_21,
  output [7:0] out_22,
  output [7:0] out_23,
  output [7:0] out_24,
  output [7:0] out_25,
  output [7:0] out_26,
  output [7:0] out_27,
  output [7:0] out_28,
  output [7:0] out_29,
  output [7:0] out_30,
  output [7:0] out_31,
  output [7:0] out_32,
  output [7:0] out_33,
  output [7:0] out_34,
  output [7:0] out_35,
  output [7:0] out_36,
  output [7:0] out_37,
  output [7:0] out_38,
  output [7:0] out_39
);

  wire cpu_decoder_4x16_1_o1, cpu_decoder_4x16_1_o2, cpu_decoder_4x16_1_o3, cpu_decoder_4x16_1_o4,
       cpu_decoder_4x16_1_o5, cpu_decoder_4x16_1_o6, cpu_decoder_4x16_1_o7, cpu_decoder_4x16_1_o8,
       cpu_decoder_4x16_1_o9, cpu_decoder_4x16_1_o10, cpu_decoder_4x16_1_o11, cpu_decoder_4x16_1_o12,
       cpu_decoder_4x16_1_o13, cpu_decoder_4x16_1_o14, cpu_decoder_4x16_1_o15, cpu_decoder_4x16_1_o16,
       cpu_decoder_4x16_2_o1, cpu_decoder_4x16_2_o2, cpu_decoder_4x16_2_o3, cpu_decoder_4x16_2_o4,
       cpu_decoder_4x16_2_o5, cpu_decoder_4x16_2_o6, cpu_decoder_4x16_2_o7, cpu_decoder_4x16_2_o8,
       cpu_decoder_4x16_2_o9, cpu_decoder_4x16_2_o10, cpu_decoder_4x16_2_o11, cpu_decoder_4x16_2_o12,
       cpu_decoder_4x16_2_o13, cpu_decoder_4x16_2_o14, cpu_decoder_4x16_2_o15, cpu_decoder_4x16_2_o16;
  wire [7:0] cpu_mem_8_1_o, cpu_reg_byte_1_o;

  CPU_MEM_8 cpu_mem_8_1 (.i(adress), .s(sa), .o(cpu_mem_8_1_o));
  CPU_DECODER_4x16 cpu_decoder_4x16_1 (
    .i(cpu_mem_8_1_o[7:4]), .o1(cpu_decoder_4x16_1_o1), .o2(cpu_decoder_4x16_1_o2),
    .o3(cpu_decoder_4x16_1_o3), .o4(cpu_decoder_4x16_1_o4), .o5(cpu_decoder_4x16_1_o5),
    .o6(cpu_decoder_4x16_1_o6), .o7(cpu_decoder_4x16_1_o7), .o8(cpu_decoder_4x16_1_o8),
    .o9(cpu_decoder_4x16_1_o9), .o10(cpu_decoder_4x16_1_o10), .o11(cpu_decoder_4x16_1_o11),
    .o12(cpu_decoder_4x16_1_o12), .o13(cpu_decoder_4x16_1_o13), .o14(cpu_decoder_4x16_1_o14),
    .o15(cpu_decoder_4x16_1_o15), .o16(cpu_decoder_4x16_1_o16));
  assign o = e ? cpu_reg_byte_1_o : 8'bz;  // Controlled_Buffer controlled_buffer_1
  CPU_REG_BYTE cpu_reg_byte_1 (
    .i(i), .h(cpu_decoder_4x16_1_o1), .v(cpu_decoder_4x16_2_o16), .s(s), .e(e), .reset(reset), .op(out_8),
    .o(cpu_reg_byte_1_o));
  CPU_REG_BYTE cpu_reg_byte_2 (
    .i(i), .h(cpu_decoder_4x16_1_o2), .v(cpu_decoder_4x16_2_o16), .s(s), .e(e), .reset(reset), .op(out_24),
    .o(cpu_reg_byte_1_o));
  CPU_DECODER_4x16 cpu_decoder_4x16_2 (
    .i(cpu_mem_8_1_o[3:0]), .o1(cpu_decoder_4x16_2_o1), .o2(cpu_decoder_4x16_2_o2),
    .o3(cpu_decoder_4x16_2_o3), .o4(cpu_decoder_4x16_2_o4), .o5(cpu_decoder_4x16_2_o5),
    .o6(cpu_decoder_4x16_2_o6), .o7(cpu_decoder_4x16_2_o7), .o8(cpu_decoder_4x16_2_o8),
    .o9(cpu_decoder_4x16_2_o9), .o10(cpu_decoder_4x16_2_o10), .o11(cpu_decoder_4x16_2_o11),
    .o12(cpu_decoder_4x16_2_o12), .o13(cpu_decoder_4x16_2_o13), .o14(cpu_decoder_4x16_2_o14),
    .o15(cpu_decoder_4x16_2_o15), .o16(cpu_decoder_4x16_2_o16));
  CPU_REG_BYTE cpu_reg_byte_3 (
    .i(i), .h(cpu_decoder_4x16_1_o1), .v(cpu_decoder_4x16_2_o15), .s(s), .e(e), .reset(reset), .op(out_9),
    .o(cpu_reg_byte_1_o));
  CPU_REG_BYTE cpu_reg_byte_4 (
    .i(i), .h(cpu_decoder_4x16_1_o2), .v(cpu_decoder_4x16_2_o15), .s(s), .e(e), .reset(reset), .op(out_25),
    .o(cpu_reg_byte_1_o));
  CPU_REG_BYTE cpu_reg_byte_5 (
    .i(i), .h(cpu_decoder_4x16_1_o1), .v(cpu_decoder_4x16_2_o14), .s(s), .e(e), .reset(reset), .op(out_10),
    .o(cpu_reg_byte_1_o));
  CPU_REG_BYTE cpu_reg_byte_6 (
    .i(i), .h(cpu_decoder_4x16_1_o2), .v(cpu_decoder_4x16_2_o14), .s(s), .e(e), .reset(reset), .op(out_26),
    .o(cpu_reg_byte_1_o));
  CPU_REG_BYTE cpu_reg_byte_7 (
    .i(i), .h(cpu_decoder_4x16_1_o1), .v(cpu_decoder_4x16_2_o13), .s(s), .e(e), .reset(reset), .op(out_11),
    .o(cpu_reg_byte_1_o));
  CPU_REG_BYTE cpu_reg_byte_8 (
    .i(i), .h(cpu_decoder_4x16_1_o2), .v(cpu_decoder_4x16_2_o13), .s(s), .e(e), .reset(reset), .op(out_27),
    .o(cpu_reg_byte_1_o));
  CPU_REG_BYTE cpu_reg_byte_9 (
    .i(i), .h(cpu_decoder_4x16_1_o1), .v(cpu_decoder_4x16_2_o12), .s(s), .e(e), .reset(reset), .op(out_12),
    .o(cpu_reg_byte_1_o));
  CPU_REG_BYTE cpu_reg_byte_10 (
    .i(i), .h(cpu_decoder_4x16_1_o2), .v(cpu_decoder_4x16_2_o12), .s(s), .e(e), .reset(reset), .op(out_28),
    .o(cpu_reg_byte_1_o));
  CPU_REG_BYTE cpu_reg_byte_11 (
    .i(i), .h(cpu_decoder_4x16_1_o1), .v(cpu_decoder_4x16_2_o11), .s(s), .e(e), .reset(reset), .op(out_13),
    .o(cpu_reg_byte_1_o));
  CPU_REG_BYTE cpu_reg_byte_12 (
    .i(i), .h(cpu_decoder_4x16_1_o2), .v(cpu_decoder_4x16_2_o11), .s(s), .e(e), .reset(reset), .op(out_29),
    .o(cpu_reg_byte_1_o));
  CPU_REG_BYTE cpu_reg_byte_13 (
    .i(i), .h(cpu_decoder_4x16_1_o1), .v(cpu_decoder_4x16_2_o10), .s(s), .e(e), .reset(reset), .op(out_14),
    .o(cpu_reg_byte_1_o));
  CPU_REG_BYTE cpu_reg_byte_14 (
    .i(i), .h(cpu_decoder_4x16_1_o2), .v(cpu_decoder_4x16_2_o10), .s(s), .e(e), .reset(reset), .op(out_30),
    .o(cpu_reg_byte_1_o));
  CPU_REG_BYTE cpu_reg_byte_15 (
    .i(i), .h(cpu_decoder_4x16_1_o1), .v(cpu_decoder_4x16_2_o9), .s(s), .e(e), .reset(reset), .op(out_15),
    .o(cpu_reg_byte_1_o));
  CPU_REG_BYTE cpu_reg_byte_16 (
    .i(i), .h(cpu_decoder_4x16_1_o2), .v(cpu_decoder_4x16_2_o9), .s(s), .e(e), .reset(reset), .op(out_31),
    .o(cpu_reg_byte_1_o));
  CPU_REG_BYTE cpu_reg_byte_17 (
    .i(i), .h(cpu_decoder_4x16_1_o1), .v(cpu_decoder_4x16_2_o8), .s(s), .e(e), .reset(reset), .op(out_16),
    .o(cpu_reg_byte_1_o));
  CPU_REG_BYTE cpu_reg_byte_18 (
    .i(i), .h(cpu_decoder_4x16_1_o2), .v(cpu_decoder_4x16_2_o8), .s(s), .e(e), .reset(reset), .op(out_32),
    .o(cpu_reg_byte_1_o));
  CPU_REG_BYTE cpu_reg_byte_19 (
    .i(i), .h(cpu_decoder_4x16_1_o1), .v(cpu_decoder_4x16_2_o7), .s(s), .e(e), .reset(reset), .op(out_17),
    .o(cpu_reg_byte_1_o));
  CPU_REG_BYTE cpu_reg_byte_20 (
    .i(i), .h(cpu_decoder_4x16_1_o2), .v(cpu_decoder_4x16_2_o7), .s(s), .e(e), .reset(reset), .op(out_33),
    .o(cpu_reg_byte_1_o));
  CPU_REG_BYTE cpu_reg_byte_21 (
    .i(i), .h(cpu_decoder_4x16_1_o1), .v(cpu_decoder_4x16_2_o6), .s(s), .e(e), .reset(reset), .op(out_18),
    .o(cpu_reg_byte_1_o));
  CPU_REG_BYTE cpu_reg_byte_22 (
    .i(i), .h(cpu_decoder_4x16_1_o2), .v(cpu_decoder_4x16_2_o6), .s(s), .e(e), .reset(reset), .op(out_34),
    .o(cpu_reg_byte_1_o));
  CPU_REG_BYTE cpu_reg_byte_23 (
    .i(i), .h(cpu_decoder_4x16_1_o1), .v(cpu_decoder_4x16_2_o5), .s(s), .e(e), .reset(reset), .op(out_19),
    .o(cpu_reg_byte_1_o));
  CPU_REG_BYTE cpu_reg_byte_24 (
    .i(i), .h(cpu_decoder_4x16_1_o2), .v(cpu_decoder_4x16_2_o5), .s(s), .e(e), .reset(reset), .op(out_35),
    .o(cpu_reg_byte_1_o));
  CPU_REG_BYTE cpu_reg_byte_25 (
    .i(i), .h(cpu_decoder_4x16_1_o1), .v(cpu_decoder_4x16_2_o4), .s(s), .e(e), .reset(reset), .op(out_20),
    .o(cpu_reg_byte_1_o));
  CPU_REG_BYTE cpu_reg_byte_26 (
    .i(i), .h(cpu_decoder_4x16_1_o2), .v(cpu_decoder_4x16_2_o4), .s(s), .e(e), .reset(reset), .op(out_36),
    .o(cpu_reg_byte_1_o));
  CPU_REG_BYTE cpu_reg_byte_27 (
    .i(i), .h(cpu_decoder_4x16_1_o1), .v(cpu_decoder_4x16_2_o3), .s(s), .e(e), .reset(reset), .op(out_21),
    .o(cpu_reg_byte_1_o));
  CPU_REG_BYTE cpu_reg_byte_28 (
    .i(i), .h(cpu_decoder_4x16_1_o2), .v(cpu_decoder_4x16_2_o3), .s(s), .e(e), .reset(reset), .op(out_37),
    .o(cpu_reg_byte_1_o));
  CPU_REG_BYTE cpu_reg_byte_29 (
    .i(i), .h(cpu_decoder_4x16_1_o1), .v(cpu_decoder_4x16_2_o2), .s(s), .e(e), .reset(reset), .op(out_22),
    .o(cpu_reg_byte_1_o));
  CPU_REG_BYTE cpu_reg_byte_30 (
    .i(i), .h(cpu_decoder_4x16_1_o2), .v(cpu_decoder_4x16_2_o2), .s(s), .e(e), .reset(reset), .op(out_38),
    .o(cpu_reg_byte_1_o));
  CPU_REG_BYTE cpu_reg_byte_31 (
    .i(i), .h(cpu_decoder_4x16_1_o1), .v(cpu_decoder_4x16_2_o1), .s(s), .e(e), .reset(reset), .op(out_23),
    .o(cpu_reg_byte_1_o));
  CPU_REG_BYTE cpu_reg_byte_32 (
    .i(i), .h(cpu_decoder_4x16_1_o2), .v(cpu_decoder_4x16_2_o1), .s(s), .e(e), .reset(reset), .op(out_39),
    .o(cpu_reg_byte_1_o));

  // Notes on the sheet:
  //   sa: pull=down
  //   adress: pull=down
  //   s: pull=down
  //   e: pull=down
  //   i: pull=down
  //   o: pull=down
endmodule

module ALU_ADDER (
  input  a,
  input  b,
  input  carry_in,
  output sum,
  output carry_out
);

  wire and_1_out, and_2_out, and_3_out, and_4_out, and_5_out, and_6_out, and_7_out, not_1_out, not_2_out,
       not_3_out;

  not not_1 (not_1_out, a);
  not not_2 (not_2_out, b);
  not not_3 (not_3_out, carry_in);
  and and_1 (and_1_out, not_1_out, not_2_out, carry_in);
  and and_2 (and_2_out, not_1_out, b, not_3_out);
  and and_3 (and_3_out, a, not_2_out, not_3_out);
  and and_4 (and_4_out, a, b, carry_in);
  and and_5 (and_5_out, b, carry_in);
  and and_6 (and_6_out, a, carry_in);
  and and_7 (and_7_out, a, b);
  or or_1 (sum, and_1_out, and_2_out, and_3_out, and_4_out);
  or or_2 (carry_out, and_5_out, and_6_out, and_7_out);
endmodule

module ALU_ADDER_8 (
  input  [7:0] a,
  input  carry_in,
  input  [7:0] b,
  output [7:0] sum,
  output carry_out
);

  wire alu_adder_1_carry_out, alu_adder_2_carry_out, alu_adder_3_carry_out, alu_adder_4_carry_out,
       alu_adder_5_carry_out, alu_adder_6_carry_out, alu_adder_7_carry_out;

  ALU_ADDER alu_adder_1 (.carry_in(carry_in), .a(a[0]), .b(b[0]), .sum(sum[0]), .carry_out(alu_adder_1_carry_out));
  ALU_ADDER alu_adder_2 (
    .carry_in(alu_adder_1_carry_out), .a(a[1]), .b(b[1]), .sum(sum[1]), .carry_out(alu_adder_2_carry_out));
  ALU_ADDER alu_adder_3 (
    .carry_in(alu_adder_2_carry_out), .a(a[2]), .b(b[2]), .sum(sum[2]), .carry_out(alu_adder_3_carry_out));
  ALU_ADDER alu_adder_4 (
    .carry_in(alu_adder_3_carry_out), .a(a[3]), .b(b[3]), .sum(sum[3]), .carry_out(alu_adder_4_carry_out));
  ALU_ADDER alu_adder_5 (
    .carry_in(alu_adder_4_carry_out), .a(a[4]), .b(b[4]), .sum(sum[4]), .carry_out(alu_adder_5_carry_out));
  ALU_ADDER alu_adder_6 (
    .carry_in(alu_adder_5_carry_out), .a(a[5]), .b(b[5]), .sum(sum[5]), .carry_out(alu_adder_6_carry_out));
  ALU_ADDER alu_adder_7 (
    .carry_in(alu_adder_6_carry_out), .a(a[6]), .b(b[6]), .sum(sum[6]), .carry_out(alu_adder_7_carry_out));
  ALU_ADDER alu_adder_8 (.carry_in(alu_adder_7_carry_out), .a(a[7]), .b(b[7]), .sum(sum[7]), .carry_out(carry_out));
endmodule

module ALU_SHIFT_L (
  input  shift_in,
  input  [7:0] i,
  output [7:0] o,
  output shift_out
);


  assign o = {i[6:0], shift_in};
  assign shift_out = i[7];
endmodule

module ALU_SHIFT_R (
  input  [7:0] i,
  input  shift_in,
  output shift_out,
  output [7:0] o
);


  assign o = {shift_in, i[7:1]};
  assign shift_out = i[0];
endmodule

module ALU_NOT (
  input  [7:0] i,
  output [7:0] not_8
);

  not not_1 (not_8[0], i[0]);
  not not_2 (not_8[1], i[1]);
  not not_3 (not_8[2], i[2]);
  not not_4 (not_8[3], i[3]);
  not not_5 (not_8[4], i[4]);
  not not_6 (not_8[5], i[5]);
  not not_7 (not_8[6], i[6]);
  not u_not_8 (not_8[7], i[7]);
endmodule

module ALU_AND (
  input  [7:0] a,
  input  [7:0] b,
  output [7:0] and_8
);

  and and_1 (and_8[0], a[0], b[0]);
  and and_2 (and_8[1], a[1], b[1]);
  and and_3 (and_8[2], a[2], b[2]);
  and and_4 (and_8[3], a[3], b[3]);
  and and_5 (and_8[4], a[4], b[4]);
  and and_6 (and_8[5], a[5], b[5]);
  and and_7 (and_8[6], a[6], b[6]);
  and u_and_8 (and_8[7], a[7], b[7]);
endmodule

module ALU_OR (
  input  [7:0] a,
  input  [7:0] b,
  output [7:0] or_8
);

  or or_1 (or_8[0], a[0], b[0]);
  or or_2 (or_8[1], a[1], b[1]);
  or or_3 (or_8[2], a[2], b[2]);
  or or_4 (or_8[3], a[3], b[3]);
  or or_5 (or_8[4], a[4], b[4]);
  or or_6 (or_8[5], a[5], b[5]);
  or or_7 (or_8[6], a[6], b[6]);
  or u_or_8 (or_8[7], a[7], b[7]);
endmodule

module ALU_XOR_LE (
  input  [7:0] a,
  input  [7:0] b,
  output larger,
  output equal,
  output [7:0] xor_8
);

  Comparator #(.mode("unsigned")) comparator_1 (.a(a), .b(b), .gt(larger), .eq(equal));  // open: lt
  xor xor_1 (xor_8[0], a[0], b[0]);
  xor xor_2 (xor_8[1], a[1], b[1]);
  xor xor_3 (xor_8[2], a[2], b[2]);
  xor xor_4 (xor_8[3], a[3], b[3]);
  xor xor_5 (xor_8[4], a[4], b[4]);
  xor xor_6 (xor_8[5], a[5], b[5]);
  xor xor_7 (xor_8[6], a[6], b[6]);
  xor u_xor_8 (xor_8[7], a[7], b[7]);
endmodule

module ALU_ZERO (
  input  [7:0] i,
  output o
);

  wire or_1_out;

  or or_1 (or_1_out, i[0], i[1], i[2], i[3], i[4], i[5], i[6], i[7]);
  not not_1 (o, or_1_out);
endmodule

module CPU_ALU (
  input  [7:0] a,
  input  [7:0] b,
  input  carry_in,
  input  c2,
  input  c1,
  input  c0,
  output larger,
  output equal,
  output zero,
  output [7:0] o,
  output carry_out
);

  wire alu_adder_8_1_carry_out, alu_shift_l_1_shift_out, alu_shift_r_1_shift_out, cpu_decoder_3x8_1_o1,
       cpu_decoder_3x8_1_o2, cpu_decoder_3x8_1_o3, cpu_decoder_3x8_1_o4, cpu_decoder_3x8_1_o5,
       cpu_decoder_3x8_1_o6, cpu_decoder_3x8_1_o7;
  wire [7:0] alu_adder_8_1_sum, alu_and_1_and_8, alu_not_1_not_8, alu_or_1_or_8, alu_shift_l_1_o,
       alu_shift_r_1_o, alu_xor_le_1_xor_8;

  ALU_XOR_LE alu_xor_le_1 (.a(a), .b(b), .larger(larger), .equal(equal), .xor_8(alu_xor_le_1_xor_8));
  ALU_OR alu_or_1 (.a(a), .b(b), .or_8(alu_or_1_or_8));
  ALU_AND alu_and_1 (.a(a), .b(b), .and_8(alu_and_1_and_8));
  ALU_NOT alu_not_1 (.i(a), .not_8(alu_not_1_not_8));
  ALU_SHIFT_L alu_shift_l_1 (.shift_in(carry_in), .i(a), .o(alu_shift_l_1_o), .shift_out(alu_shift_l_1_shift_out));
  ALU_SHIFT_R alu_shift_r_1 (.i(a), .shift_in(carry_in), .shift_out(alu_shift_r_1_shift_out), .o(alu_shift_r_1_o));
  ALU_ADDER_8 alu_adder_8_1 (
    .a(a), .carry_in(carry_in), .b(b), .sum(alu_adder_8_1_sum), .carry_out(alu_adder_8_1_carry_out));
  CPU_DECODER_3x8 cpu_decoder_3x8_1 (
    .c(c0), .a(c2), .b(c1), .o3(cpu_decoder_3x8_1_o3), .o4(cpu_decoder_3x8_1_o4), .o5(cpu_decoder_3x8_1_o5),
    .o6(cpu_decoder_3x8_1_o6), .o7(cpu_decoder_3x8_1_o7), .o1(cpu_decoder_3x8_1_o1), .o2(cpu_decoder_3x8_1_o2));  // open: o8
  assign carry_out = cpu_decoder_3x8_1_o3 ? alu_shift_l_1_shift_out : 1'bz;  // Controlled_Buffer controlled_buffer_1
  assign carry_out = cpu_decoder_3x8_1_o2 ? alu_shift_r_1_shift_out : 1'bz;  // Controlled_Buffer controlled_buffer_2
  assign carry_out = cpu_decoder_3x8_1_o1 ? alu_adder_8_1_carry_out : 1'bz;  // Controlled_Buffer controlled_buffer_3
  CPU_ENABLE_8 cpu_enable_8_1 (.i(alu_xor_le_1_xor_8), .e(cpu_decoder_3x8_1_o7), .o(o));
  CPU_ENABLE_8 cpu_enable_8_2 (.i(alu_or_1_or_8), .e(cpu_decoder_3x8_1_o6), .o(o));
  CPU_ENABLE_8 cpu_enable_8_3 (.i(alu_and_1_and_8), .e(cpu_decoder_3x8_1_o5), .o(o));
  CPU_ENABLE_8 cpu_enable_8_4 (.i(alu_not_1_not_8), .e(cpu_decoder_3x8_1_o4), .o(o));
  CPU_ENABLE_8 cpu_enable_8_5 (.i(alu_shift_l_1_o), .e(cpu_decoder_3x8_1_o3), .o(o));
  CPU_ENABLE_8 cpu_enable_8_6 (.i(alu_shift_r_1_o), .e(cpu_decoder_3x8_1_o2), .o(o));
  CPU_ENABLE_8 cpu_enable_8_7 (.i(alu_adder_8_1_sum), .e(cpu_decoder_3x8_1_o1), .o(o));
  ALU_ZERO alu_zero_1 (.i(o), .o(zero));

  // Notes on the sheet:
  //   zero: pull=down
  //   a: pull=down
  //   b: pull=down
  //   carry_in: pull=down
  //   c2: pull=down
  //   c1: pull=down
  //   c0: pull=down
  //   o: pull=down
  //   carry_out: pull=down
  //   larger: pull=down
  //   equal: pull=down
endmodule

module CPU_CLK (
  output clk,
  output clk_e,
  output clk_s
);

  wire clk2_out;

  Clock #(.highDuration(2), .lowDuration(2), .phaseOffset(2)) clk1 (.out(clk));
  Clock #(.highDuration(2), .lowDuration(2), .phaseOffset(1)) clk2 (.out(clk2_out));
  or or_1 (clk_e, clk, clk2_out);
  and and_1 (clk_s, clk, clk2_out);
endmodule

module CPU_ACCUMULATOR (
  input  [7:0] i,
  input  s,
  input  e,
  output [7:0] o
);

  CPU_REG_8 cpu_reg_8_1 (.i(i), .s(s), .e(e), .o(o));  // open: r

  // Notes on the sheet:
  //   i: pull=down
  //   s: pull=down
  //   e: pull=down
  //   o: pull=down
endmodule

module CPU_TMP (
  input  [7:0] i,
  input  s,
  output [7:0] o
);

  CPU_MEM_8 cpu_mem_8_1 (.i(i), .s(s), .o(o));

  // Notes on the sheet:
  //   i: pull=down
endmodule

module CPU_BUS_1 (
  input  [7:0] i,
  input  bus1,
  output [7:0] o
);

  wire not_1_out;

  and and_1 (o[7], i[7], not_1_out);
  and and_2 (o[6], i[6], not_1_out);
  and and_3 (o[5], i[5], not_1_out);
  and and_4 (o[4], i[4], not_1_out);
  and and_5 (o[3], i[3], not_1_out);
  and and_6 (o[2], i[2], not_1_out);
  and and_7 (o[1], i[1], not_1_out);
  not not_1 (not_1_out, bus1);
  or or_1 (o[0], i[0], bus1);

  // Notes on the sheet:
  //   i: pull=down
endmodule

module CPU_REG (
  input  [7:0] i,
  input  s,
  input  e,
  output [7:0] o
);

  CPU_REG_8 cpu_reg_8_1 (.i(i), .s(s), .e(e), .o(o));  // open: r

  // Notes on the sheet:
  //   i: pull=down
endmodule

module CS_STEPPER (
  input  reset,
  input  clk,
  output step1,
  output step2,
  output step3,
  output step4,
  output step5,
  output step6,
  output step7
);

  wire cpu_mem_1_1_o, cpu_mem_1_2_o, cpu_mem_1_3_o, cpu_mem_1_4_o, cpu_mem_1_5_o, cpu_mem_1_6_o,
       cpu_mem_1_7_o, cpu_mem_1_8_o, cpu_mem_1_9_o, cpu_mem_1_10_o, cpu_mem_1_11_o, not_1_out, not_2_out,
       not_3_out, not_4_out, not_5_out, not_6_out, not_7_out, not_8_out, or_1_out, or_2_out;

  not not_1 (not_1_out, clk);
  not not_2 (not_2_out, reset);
  or or_1 (or_1_out, reset, not_1_out);
  or or_2 (or_2_out, reset, clk);
  or or_3 (step1, reset, not_3_out);
  CPU_MEM_1 cpu_mem_1_1 (.i(not_2_out), .s(or_1_out), .o(cpu_mem_1_1_o));
  not not_3 (not_3_out, cpu_mem_1_2_o);
  CPU_MEM_1 cpu_mem_1_2 (.i(cpu_mem_1_1_o), .s(or_2_out), .o(cpu_mem_1_2_o));
  and and_1 (step2, cpu_mem_1_2_o, not_4_out);
  not not_4 (not_4_out, cpu_mem_1_4_o);
  CPU_MEM_1 cpu_mem_1_3 (.i(cpu_mem_1_2_o), .s(or_1_out), .o(cpu_mem_1_3_o));
  CPU_MEM_1 cpu_mem_1_4 (.i(cpu_mem_1_3_o), .s(or_2_out), .o(cpu_mem_1_4_o));
  and and_2 (step3, cpu_mem_1_4_o, not_5_out);
  CPU_MEM_1 cpu_mem_1_5 (.i(cpu_mem_1_4_o), .s(or_1_out), .o(cpu_mem_1_5_o));
  not not_5 (not_5_out, cpu_mem_1_6_o);
  CPU_MEM_1 cpu_mem_1_6 (.i(cpu_mem_1_5_o), .s(or_2_out), .o(cpu_mem_1_6_o));
  and and_3 (step4, cpu_mem_1_6_o, not_6_out);
  not not_6 (not_6_out, cpu_mem_1_8_o);
  CPU_MEM_1 cpu_mem_1_7 (.i(cpu_mem_1_6_o), .s(or_1_out), .o(cpu_mem_1_7_o));
  CPU_MEM_1 cpu_mem_1_8 (.i(cpu_mem_1_7_o), .s(or_2_out), .o(cpu_mem_1_8_o));
  and and_4 (step5, cpu_mem_1_8_o, not_7_out);
  CPU_MEM_1 cpu_mem_1_9 (.i(cpu_mem_1_8_o), .s(or_1_out), .o(cpu_mem_1_9_o));
  not not_7 (not_7_out, cpu_mem_1_10_o);
  CPU_MEM_1 cpu_mem_1_10 (.i(cpu_mem_1_9_o), .s(or_2_out), .o(cpu_mem_1_10_o));
  and and_5 (step6, cpu_mem_1_10_o, not_8_out);
  not not_8 (not_8_out, step7);
  CPU_MEM_1 cpu_mem_1_11 (.i(cpu_mem_1_10_o), .s(or_1_out), .o(cpu_mem_1_11_o));
  CPU_MEM_1 cpu_mem_1_12 (.i(cpu_mem_1_11_o), .s(or_2_out), .o(step7));
endmodule

module CPU_IAR (
  input  [7:0] i,
  input  s,
  input  e,
  output [7:0] o
);

  CPU_REG_8 cpu_reg_8_1 (.i(i), .s(s), .e(e), .o(o));  // open: r

  // Notes on the sheet:
  //   i: pull=down
  //   s: pull=down
  //   e: pull=down
  //   o: pull=down
endmodule

module CPU_IR (
  input  [7:0] i,
  input  s,
  output [7:0] o
);

  CPU_MEM_8 cpu_mem_8_1 (.i(i), .s(s), .o(o));

  // Notes on the sheet:
  //   s: pull=down
  //   i: pull=down
  //   o: pull=down
endmodule

module FLAGS (
  input  C_in,
  input  A_in,
  input  E_in,
  input  Z_in,
  input  s,
  output C,
  output A,
  output E,
  output Z
);

  CPU_MEM_1 cpu_mem_1_1 (.i(C_in), .s(s), .o(C));
  CPU_MEM_1 cpu_mem_1_2 (.i(A_in), .s(s), .o(A));
  CPU_MEM_1 cpu_mem_1_3 (.i(E_in), .s(s), .o(E));
  CPU_MEM_1 cpu_mem_1_4 (.i(Z_in), .s(s), .o(Z));
endmodule

module C_TMP (
  input  C,
  input  s,
  output o
);

  CPU_MEM_1 cpu_mem_1_1 (.i(C), .s(s), .o(o));
endmodule

module CONTROL_SECTION (
  input  C,
  input  A,
  input  E,
  input  Z,
  input  clke,
  input  clk,
  input  clks,
  input  reset,
  output MAR_S,
  output ACC_S,
  output RAM_S,
  output TMP_S,
  output IR_S,
  output IAR_S,
  output ALU_2,
  output ALU_1,
  output ALU_0,
  output R0_S,
  output FLAGs,
  output R1_S,
  output R2_S,
  output R3_E,
  output R3_S,
  output R2_E,
  output R1_E,
  output END_end,
  output R0_E,
  output BUS_1,
  output RAM_E,
  output ACC_E,
  output IAR_E
);

  wire cs_stepper_1_step1, cs_stepper_1_step2, cs_stepper_1_step3, cs_stepper_1_step4, cs_stepper_1_step5,
       cs_stepper_1_step6, cs_stepper_1_step7, or_1_out;

  CS_STEPPER cs_stepper_1 (
    .clk(clk), .reset(or_1_out), .step4(cs_stepper_1_step4), .step5(cs_stepper_1_step5),
    .step6(cs_stepper_1_step6), .step7(cs_stepper_1_step7), .step1(cs_stepper_1_step1),
    .step2(cs_stepper_1_step2), .step3(cs_stepper_1_step3));
  or or_1 (or_1_out, reset, cs_stepper_1_step7);
endmodule

module CPU (
  input  reset
);

  wire and_1_out, c_tmp_1_o, control_section_1_acc_e, control_section_1_acc_s, control_section_1_alu_0,
       control_section_1_alu_1, control_section_1_alu_2, control_section_1_bus_1, control_section_1_flags,
       control_section_1_iar_e, control_section_1_iar_s, control_section_1_ir_s, control_section_1_mar_s,
       control_section_1_r0_e, control_section_1_r0_s, control_section_1_r1_e, control_section_1_r1_s,
       control_section_1_r2_e, control_section_1_r2_s, control_section_1_r3_e, control_section_1_r3_s,
       control_section_1_ram_e, control_section_1_ram_s, control_section_1_tmp_s, cpu_alu_1_carry_out,
       cpu_alu_1_equal, cpu_alu_1_larger, cpu_alu_1_zero, cpu_clk_1_clk, cpu_clk_1_clk_e, cpu_clk_1_clk_s,
       flags_1_a, flags_1_c, flags_1_e, flags_1_z, undriven;
  wire [7:0] cpu_accumulator_1_o, cpu_alu_1_o, cpu_bus_1_1_o, cpu_ir_1_o, cpu_tmp_1_o;

  CPU_ACCUMULATOR cpu_accumulator_1 (
    .i(cpu_alu_1_o), .s(control_section_1_acc_s), .e(control_section_1_acc_e), .o(cpu_accumulator_1_o));
  CPU_TMP cpu_tmp_1 (.s(control_section_1_tmp_s), .i(cpu_accumulator_1_o), .o(cpu_tmp_1_o));
  CPU_BUS_1 cpu_bus_1_1 (.i(cpu_tmp_1_o), .bus1(control_section_1_bus_1), .o(cpu_bus_1_1_o));
  and and_1 (and_1_out, c_tmp_1_o, undriven);
  CPU_ALU cpu_alu_1 (
    .a(cpu_accumulator_1_o), .b(cpu_bus_1_1_o), .carry_in(and_1_out), .c2(control_section_1_alu_2),
    .c1(control_section_1_alu_1), .c0(control_section_1_alu_0), .zero(cpu_alu_1_zero), .o(cpu_alu_1_o),
    .carry_out(cpu_alu_1_carry_out), .larger(cpu_alu_1_larger), .equal(cpu_alu_1_equal));
  CPU_CLK cpu_clk_1 (.clk(cpu_clk_1_clk), .clk_e(cpu_clk_1_clk_e), .clk_s(cpu_clk_1_clk_s));
  C_TMP c_tmp_1 (.C(flags_1_c), .s(control_section_1_tmp_s), .o(c_tmp_1_o));
  FLAGS flags_1 (
    .C_in(cpu_alu_1_carry_out), .A_in(cpu_alu_1_larger), .E_in(cpu_alu_1_equal), .Z_in(cpu_alu_1_zero),
    .s(control_section_1_flags), .C(flags_1_c), .A(flags_1_a), .E(flags_1_e), .Z(flags_1_z));
  CPU_REG cpu_reg_1 (
    .s(control_section_1_r0_s), .e(control_section_1_r0_e), .i(cpu_accumulator_1_o), .o(cpu_accumulator_1_o));
  CONTROL_SECTION control_section_1 (
    .reset(reset), .C(flags_1_c), .A(flags_1_a), .E(flags_1_e), .Z(flags_1_z), .clke(cpu_clk_1_clk_e),
    .clk(cpu_clk_1_clk), .clks(cpu_clk_1_clk_s), .R1_E(control_section_1_r1_e),
    .R0_E(control_section_1_r0_e), .BUS_1(control_section_1_bus_1), .RAM_E(control_section_1_ram_e),
    .ACC_E(control_section_1_acc_e), .IAR_E(control_section_1_iar_e), .MAR_S(control_section_1_mar_s),
    .ACC_S(control_section_1_acc_s), .RAM_S(control_section_1_ram_s), .TMP_S(control_section_1_tmp_s),
    .IR_S(control_section_1_ir_s), .IAR_S(control_section_1_iar_s), .ALU_2(control_section_1_alu_2),
    .ALU_1(control_section_1_alu_1), .ALU_0(control_section_1_alu_0), .FLAGs(control_section_1_flags),
    .R3_E(control_section_1_r3_e), .R2_E(control_section_1_r2_e), .R0_S(control_section_1_r0_s),
    .R1_S(control_section_1_r1_s), .R2_S(control_section_1_r2_s), .R3_S(control_section_1_r3_s));  // open: END_end
  CPU_IAR cpu_iar_1 (
    .i(cpu_accumulator_1_o), .s(control_section_1_iar_s), .e(control_section_1_iar_e), .o(cpu_accumulator_1_o));
  CPU_REG cpu_reg_2 (
    .s(control_section_1_r1_s), .e(control_section_1_r1_e), .i(cpu_accumulator_1_o), .o(cpu_accumulator_1_o));
  CPU_IR cpu_ir_1 (.s(control_section_1_ir_s), .i(cpu_accumulator_1_o), .o(cpu_ir_1_o));
  CPU_REG cpu_reg_3 (
    .s(control_section_1_r2_s), .e(control_section_1_r2_e), .i(cpu_accumulator_1_o), .o(cpu_accumulator_1_o));
  CPU_REG cpu_reg_4 (
    .s(control_section_1_r3_s), .e(control_section_1_r3_e), .i(cpu_accumulator_1_o), .o(cpu_accumulator_1_o));
  CPU_RAM_32 cpu_ram_32_1 (
    .sa(control_section_1_mar_s), .adress(cpu_accumulator_1_o), .s(control_section_1_ram_s),
    .e(control_section_1_ram_e), .reset(reset), .i(cpu_accumulator_1_o), .o(cpu_accumulator_1_o));  // open: out_9, out_25, out_10, out_26, out_11, out_27, out_12, out_28, out_13, out_29, out_14, out_30, out_15, out_31, out_16, out_32, out_17, out_33, out_18, out_34, out_19, out_35, out_20, out_36, out_21, out_37, out_22, out_38, out_23, out_39, out_8, out_24
endmodule
